# Fritzing sketch sketch1 (saved by Fritzing 0.9.3b)

parts:
  Часть2 = Arduino Nano (Rev3.0)
  R1 = Resistor [tolerance=±1% resistance=150 package=THT]
  LED1 = LED - 5mm [color="Infrared (850nm)" package="5 mm [THT]"]
  LED2 = smd LED [color="Green (555nm)" package="1206 [SMD]"]
  S2 = Momentary Switch [package=ksa_sealed_tac_switch]
  R2 = Resistor [tolerance=±1% resistance=180 package=THT]

nets:
  N1: Часть2.GND, LED1.cathode, LED2.cathode, S2.2
  N2: Часть2.D2, S2.4
  N3: Часть2.D5, R1.Pin_1
  N4: Часть2.D6, R2.Pin_1
  N5: R1.Pin_0, LED2.anode
  N6: LED1.anode, R2.Pin_0

notes:
  кнопка имеет INPUT_PULLUP
