# Fritzing sketch sketch2 (saved by Fritzing 0.9.3b)

parts:
  Часть1 = Arduino Nano (Rev3.0)
  IR1 = TSOP312.., 314.. [package=THT]
  7_Segment1 = 7 Segment Display

nets:
  GND: Часть1.GND, IR1.GND, 7_Segment1.common_cathode
  N1: Часть1.D2, 7_Segment1.Segment_A
  N2: Часть1.D3, 7_Segment1.Segment_B
  N3: Часть1.D4, 7_Segment1.Segment_C
  N4: Часть1.D5, 7_Segment1.Segment_D
  N5: Часть1.D6, 7_Segment1.Segment_E
  N6: Часть1.D7, 7_Segment1.Segment_F
  N7: Часть1.D8, 7_Segment1.Segment_G
  N8: Часть1.D9, 7_Segment1.Segment_DP
  N9: Часть1.5V, IR1.Vs
  N10: Часть1.A0, IR1.Data

notes:
  у нас был другой приёмник:
  Data, Gnd, Vcc
