# Fritzing sketch sketch3 (saved by Fritzing 0.9.3b)

parts:
  Часть1 = Soil Moisture Sensor
  J1 = Piezo Speaker
  Часть2 = Arduino Nano (Rev3.0)

nets:
  N1: Часть1.SIG, Часть2.A6
  GND: Часть1.GND, J1.pin1, Часть2.GND
  VCC: Часть1.VCC, Часть2.5V
  N2: J1.pin2, Часть2.D4

notes:
  У нас был water sensor:
  Data, Vcc, Gnd
